// Logisim project 4bitfulladder.circ as structural Verilog: 1 circuit, main circuit main
module main (
  input  c0,
  input  [3:0] a,
  input  [3:0] b,
  output s0,
  output C2,
  output [4:0] out_6,
  output C3,
  output C4
);

  wire and_1_out, and_2_out, and_3_out, and_4_out, and_5_out, and_6_out, and_7_out, and_8_out, or_1_out,
       or_2_out, or_3_out, or_4_out, or_5_out, or_7_out, or_9_out, xor_1_out, xor_2_out, xor_3_out,
       xor_4_out, xor_5_out, xor_7_out, xor_8_out;

  and and_1 (and_1_out, a[3], b[3]);
  xor xor_1 (xor_1_out, a[3], b[3]);
  xor xor_2 (xor_2_out, a[3], b[3]);
  xor xor_3 (xor_3_out, a[0], b[0]);
  and and_2 (and_2_out, a[0], b[0]);
  xor xor_4 (xor_4_out, a[2], a[2]);
  xor xor_5 (xor_5_out, a[2], b[2]);
  and and_3 (and_3_out, a[2], b[2]);
  and and_4 (and_4_out, c0, xor_3_out);
  xor xor_6 (out_6[0], xor_3_out, c0);
  or or_1 (or_1_out, and_4_out, and_2_out);
  or or_2 (or_2_out, and_2_out, and_4_out);
  xor xor_7 (xor_7_out, a[1], b[1]);
  xor xor_8 (xor_8_out, a[1], b[1]);
  and and_5 (and_5_out, a[1], b[1]);
  or or_3 (or_3_out, and_4_out, and_2_out);
  or or_4 (or_4_out, and_5_out, and_6_out);
  xor xor_9 (out_6[1], or_3_out, xor_7_out);
  and and_6 (and_6_out, or_2_out, xor_8_out);
  or or_5 (or_5_out, and_5_out, and_6_out);
  and and_7 (and_7_out, or_5_out, xor_5_out);
  or or_6 (C2, and_6_out, and_5_out);
  or or_7 (or_7_out, and_3_out, and_7_out);
  xor xor_10 (out_6[2], or_4_out, xor_4_out);
  or or_8 (C3, and_7_out, and_3_out);
  buf or_9 (or_9_out, and_3_out);  // OR_Gate
  and and_8 (and_8_out, or_7_out, xor_1_out);
  xor xor_11 (out_6[3], or_9_out, xor_2_out);
  or or_10 (C4, and_8_out, and_1_out);

  assign out_6[4] = C4;
  assign s0 = out_6[0];

  // Notes on the sheet:
  //   a3
  //   b3
  //   a2
  //   b2
  //   a2
  //   g3
  //   p3
  //   p0
  //   g0
  //   b2
  //   p2
  //   g2
  //   p0c0
  //   a1
  //   b1
  //   a1
  //   b1
  //   a1
  //   b1
  //   p1
  //   p1
  //   g1
  //   C1
  //   p1c1
  //   p2c2
endmodule
